// Logisim project Contador_Inteligente.circ as structural Verilog: 3 circuits, main circuit main
module main (
  input  in_1,
  input  in_2,
  input  in_3,
  input  in_4,
  input  in_5,
  input  in_6,
  input  in_7,
  input  in_8,
  input  in_9,
  input  in_10,
  input  in_11,
  input  in_12,
  input  in_13,
  input  in_14,
  output [3:0] LSB,
  output [3:0] MSB,
  output [3:0] DEZENAS,
  output [3:0] CENTENAS,
  output [3:0] out_19,
  output [3:0] DEZENAS_2
);

  MX_MI mx_mi_1 (
    .UNIDADES_2(DEZENAS_2), .UNIDADES_3(LSB), .DEZENAS_3(CENTENAS), .DEZENAS_4(DEZENAS), .in_1(in_8),
    .out_13(MSB), .out_14(out_19), .DEZENAS({in_14, in_13, in_12, in_11}),
    .DEZENAS_2({in_14, in_13, in_12, in_11}), .UNIDADES({in_9, in_7, in_6, in_5}),
    .in_6({in_9, in_7, in_6, in_5}), .in_7({in_4, in_3, in_2, in_1}), .in_8({in_4, in_3, in_2, in_1}),
    .in_2(in_10));

  // Other names for the same wires on the sheet: A0C = in_11; A1C = in_12; A2C = in_13; A3C = in_14; A0D = in_5;
  //   A1D = in_6; A2D = in_7; A3D = in_9; A0U = in_1; A1U = in_2; A2U = in_3; A3U = in_4

  // Notes on the sheet:
  //   UNIDADES
  //   DEZENAS
  //   CENTENAS
  //   CENTENAS
  //   MSB
  //   UNIDADES
  //   LSB
  //   UNIDADES
endmodule

module Armazenador_de_bits (
  input  in_1,
  input  in_2,
  input  in_3,
  input  in_4,
  input  in_5,
  input  in_6,
  input  in_7,
  input  in_8,
  input  in_9,
  input  in_10,
  input  in_11,
  input  in_12,
  input  in_13,
  output out_14,
  output out_15,
  output out_16,
  output out_17,
  output out_18,
  output out_19,
  output out_20,
  output out_21,
  output out_22,
  output out_23,
  output out_24,
  output out_25
);

  D_Flip_Flop d_ff_1 (.clk(in_1), .D(in_2), .Q(out_14));  // open: Qn, preset, en, reset
  D_Flip_Flop d_ff_2 (.clk(in_1), .D(in_6), .Q(out_18));  // open: Qn, preset, en, reset
  D_Flip_Flop d_ff_3 (.clk(in_1), .D(in_10), .Q(out_22));  // open: Qn, preset, en, reset
  D_Flip_Flop d_ff_4 (.clk(in_1), .D(in_3), .Q(out_15));  // open: Qn, preset, en, reset
  D_Flip_Flop d_ff_5 (.clk(in_1), .D(in_7), .Q(out_19));  // open: Qn, preset, en, reset
  D_Flip_Flop d_ff_6 (.clk(in_1), .D(in_11), .Q(out_23));  // open: Qn, preset, en, reset
  D_Flip_Flop d_ff_7 (.clk(in_1), .D(in_4), .Q(out_16));  // open: Qn, preset, en, reset
  D_Flip_Flop d_ff_8 (.clk(in_1), .D(in_8), .Q(out_20));  // open: Qn, preset, en, reset
  D_Flip_Flop d_ff_9 (.clk(in_1), .D(in_12), .Q(out_24));  // open: Qn, preset, en, reset
  D_Flip_Flop d_ff_10 (.clk(in_1), .D(in_5), .Q(out_17));  // open: Qn, preset, en, reset
  D_Flip_Flop d_ff_11 (.clk(in_1), .D(in_9), .Q(out_21));  // open: Qn, preset, en, reset
  D_Flip_Flop d_ff_12 (.clk(in_1), .D(in_13), .Q(out_25));  // open: Qn, preset, en, reset

  // Other names for the same wires on the sheet: CLK = in_1

  // Notes on the sheet:
  //   A3
  //   A3
  //   A3
  //   A2
  //   A2
  //   A2
  //   A1
  //   A1
  //   A1
  //   A0
  //   A0
  //   A0
  //   A0
  //   A1
  //   A2
  //   ENTRADA DE CLK
endmodule

module MX_MI (
  input  in_1,
  input  in_2,
  input  [3:0] DEZENAS,
  input  [3:0] DEZENAS_2,
  input  [3:0] UNIDADES,
  input  [3:0] in_6,
  input  [3:0] in_7,
  input  [3:0] in_8,
  output [3:0] UNIDADES_2,
  output [3:0] UNIDADES_3,
  output [3:0] DEZENAS_3,
  output [3:0] DEZENAS_4,
  output [3:0] out_13,
  output [3:0] out_14
);

  wire and_1_out, and_2_out, not_1_out;

  and and_1 (and_1_out, in_1, in_2);
  Armazenador_de_bits armazenador_de_bits_1 (
    .out_14(UNIDADES_3[3]), .out_18(DEZENAS_4[3]), .out_22(out_14[3]), .out_15(UNIDADES_3[2]),
    .out_19(DEZENAS_4[2]), .out_23(out_14[2]), .out_16(UNIDADES_3[1]), .out_20(DEZENAS_4[1]),
    .out_24(out_14[1]), .out_17(UNIDADES_3[0]), .out_21(DEZENAS_4[0]), .out_25(out_14[0]), .in_2(in_8[3]),
    .in_6(in_6[3]), .in_10(DEZENAS_2[3]), .in_3(in_8[2]), .in_7(in_6[2]), .in_11(DEZENAS_2[2]),
    .in_4(in_8[1]), .in_8(in_6[1]), .in_12(DEZENAS_2[1]), .in_5(in_8[0]), .in_9(in_6[0]),
    .in_13(DEZENAS_2[0]), .in_1(and_1_out));
  and and_2 (and_2_out, in_1, not_1_out);
  not not_1 (not_1_out, in_2);
  Armazenador_de_bits armazenador_de_bits_2 (
    .out_14(UNIDADES_2[3]), .out_18(DEZENAS_3[3]), .out_22(out_13[3]), .out_15(UNIDADES_2[2]),
    .out_19(DEZENAS_3[2]), .out_23(out_13[2]), .out_16(UNIDADES_2[1]), .out_20(DEZENAS_3[1]),
    .out_24(out_13[1]), .out_17(UNIDADES_2[0]), .out_21(DEZENAS_3[0]), .out_25(out_13[0]), .in_2(in_7[3]),
    .in_6(UNIDADES[3]), .in_10(DEZENAS[3]), .in_3(in_7[2]), .in_7(UNIDADES[2]), .in_11(DEZENAS[2]),
    .in_4(in_7[1]), .in_8(UNIDADES[1]), .in_12(DEZENAS[1]), .in_5(in_7[0]), .in_9(UNIDADES[0]),
    .in_13(DEZENAS[0]), .in_1(and_2_out));

  // Other names for the same wires on the sheet: CLK = in_1; MX_MI = in_2

  // Notes on the sheet:
  //   CENTENAS
  //   CENTENAS
  //   UNIDADES
  //   MÁXIMO
  //   CENTENAS
  //   CENTENAS
  //   MÍNIMO
  //   ENTRADA DE CLK
  //   ENTRADA MX_MI
endmodule
